# Fritzing sketch spires (saved by Fritzing 1.0.3b)
circuit board: 5.69999cm x 6.09999cm
breadboards: 2

parts:
  Nano = Arduino Nano (Rev3.0)
  RE1 = Rotary Encoder [package=THT]
  S5 = SPST Switch [package=switch-spdt_kit]
  VCC1 = 4 x AAA Battery Mount
  LDR = Photocell (LDR) [power=0.25W dark_resistance_@0.01lx=300kΩ light_resistance_@100lx=400Ω luminance=10lx package=THT]
  100uF1 = Electrolytic Capacitor [capacitance=0.1mF voltage=35V package="100 mil [THT, electrolytic]"]
  470nf = Ceramic Capacitor [capacitance=0.47µF voltage=16V package="200 mil [THT, multilayer]"]
  4_7K = Resistor [tolerance=±5% resistance=4.7k power=0.25W package=THT]
  104 = Ceramic Capacitor [capacitance=100nF voltage=16V package="200 mil [THT, multilayer]"]
  AD9833 = female pin header, 7 pins [form="♀ (female)"]
  VL53L0/1XV2 = female pin header, 6 pins [form="♀ (female)"]
  TDA7052A = IC, DIP package, 8 pins [chip_label=IC]
  A1 = VL53lox  # not connected
  U2 = AD9833 Module  # not connected
  220 = Resistor [tolerance=±1% resistance=220 power=0.25W package=THT]
  220_2 = Resistor [tolerance=±1% resistance=220 power=0.25W package=THT]
  midi = 3.5mm Audio Jack-wq-pj320b.fzpz [package=audio-jack-3.5mm-smd]
  LED8 = LED - 3mm [color="Red (635nm)" current=0.030A package="3 mm [THT]"]
  1K = Resistor [tolerance=±5% resistance=1k power=0.25W package=THT]
  audio = 3.5mm Audio Jack-wq-pj320b.fzpz [package=audio-jack-3.5mm-smd]

nets:
  N1: Nano.D1/TX, 220.Pin_1
  AGND/DGND/GND: Nano.GND, RE1.GND, RE1.SW-2, AD9833.pin2, VL53L0/1XV2.pin2, midi.pin_4, 1K.Pin_0
  N2: Nano.D2, LED8.anode
  N3: Nano.D4, RE1.SW-1
  N4: Nano.D5, RE1.Pin-B
  N5: Nano.D6, RE1.Pin-A
  N6: Nano.D7, VL53L0/1XV2.pin6
  N7: Nano.D8, AD9833.pin5
  N8: Nano.D11/MOSI, AD9833.pin3
  N9: Nano.VIN, S5.S
  V++: Nano.5V, 100uF1.+, 104.1, AD9833.pin1, TDA7052A.pin1, 220_2.Pin_1
  N10: Nano.A5, VL53L0/1XV2.pin3
  N11: Nano.A4, VL53L0/1XV2.pin4
  N12: Nano.3V3, VL53L0/1XV2.pin1
  N13: Nano.D13/SCK, AD9833.pin4
  N14: S5.P, VCC1.+
  N15: VCC1.-, 100uF1.-, 4_7K.Pin_1, 104.0, AD9833.pin6, TDA7052A.pin3, TDA7052A.pin6, audio.pin_4
  N16: LDR.pin_0, TDA7052A.pin5
  N17: LDR.pin_1, audio.pin_2, audio.Pin_3
  N18: 470nf.0, 4_7K.Pin_0, AD9833.pin7
  N19: 470nf.1, TDA7052A.pin2
  N20: 220.Pin_0, midi.pin_2
  N21: 220_2.Pin_0, midi.Pin_3
  N22: LED8.cathode, 1K.Pin_1

notes:
  spires v1
  AD9833
  VL53L01
  jlcjlcjlcjlc
  blueprint@poetaster.de 2025

custom parts:
  Rotary Encoder: Rotary Encoder with push button
  4 x AAA Battery Mount: A 4 x AAA battery pack (4.8 Volts with recharables)
  VL53lox: VL53L0X Time-of-Flight (ToF) Laser Ranging Sensor Breakout.
  AD9833 Module: programmable waveform generator
  3.5mm Audio Jack-wq-pj320b.fzpz: 3.5mm Audio Jack WQP-PJ320B is a SMD jack, dia 1/8 inch, female, right angle and through hole.
